// Logisim project project4.circ as structural Verilog: 20 circuits, main circuit SevenSegmentDecoderTestBench
module SevenSegmentDecoderTestBench (
);

  wire sevenseg_seg_a, sevenseg_seg_b, sevenseg_seg_c, sevenseg_seg_d, sevenseg_seg_e, sevenseg_seg_f,
       sevenseg_seg_g;
  wire [3:0] BCD_sw4;

  DipSwitch #(.number(4)) BCD (.sw1(BCD_sw4[3]), .sw2(BCD_sw4[2]), .sw3(BCD_sw4[1]), .sw4(BCD_sw4[0]));
  SevenSegmentDecoder sevenseg (
    .BCDin(BCD_sw4), .seg_A(sevenseg_seg_a), .seg_B(sevenseg_seg_b), .seg_C(sevenseg_seg_c),
    .seg_D(sevenseg_seg_d), .seg_E(sevenseg_seg_e), .seg_F(sevenseg_seg_f), .seg_G(sevenseg_seg_g));
  _7_Segment_Display Implementation (
    .g(sevenseg_seg_g), .f(sevenseg_seg_f), .a(sevenseg_seg_a), .b(sevenseg_seg_b), .e(sevenseg_seg_e),
    .d(sevenseg_seg_d), .c(sevenseg_seg_c));  // open: dp
  _7_Segment_Display reference ();  // open: g, f, a, b, e, d, c, dp
  // BCD_to_7_Segment_decoder bcd_to_7_segment_decoder_1: pin names not known; wires that end beside it: BCD_sw4

  // Notes on the sheet:
  //   Implementation
  //   Reference
endmodule

module SevenSegmentDecoder (
  input  [3:0] BCDin,
  output seg_A,
  output seg_B,
  output seg_C,
  output seg_D,
  output seg_E,
  output seg_F,
  output seg_G
);

  segmentA sega (.BCDin(BCDin), .seg_A(seg_A));
  segmentB segb (.BCDin(BCDin), .seg_B(seg_B));
  segmentC segc (.BCDin(BCDin), .seg_C(seg_C));
  segmentD segd (.BCDin(BCDin), .seg_D(seg_D));
  segmentE sege (.BCDin(BCDin), .seg_E(seg_E));
  segmentF segf (.BCDin(BCDin), .seg_F(seg_F));
  segmentG segg (.BCDin(BCDin), .seg_G(seg_G));
endmodule

module segmentB (
  input  [3:0] BCDin,
  output seg_B
);

  wire nor_1_out, nor_2_out, nor_3_out, nor_4_out, nor_5_out;

  nor nor_1 (nor_1_out, BCDin[0], BCDin[0]);
  nor nor_2 (nor_2_out, BCDin[1], BCDin[1]);
  nor nor_3 (nor_3_out, BCDin[2], BCDin[2]);
  nor nor_4 (nor_4_out, nor_1_out, BCDin[1], nor_3_out);
  nor nor_5 (nor_5_out, nor_2_out, BCDin[0], nor_3_out);
  nor nor_6 (seg_B, nor_4_out, nor_5_out);

  // Other names for the same wires on the sheet: a0 = BCDin[0]; a1 = BCDin[1]; a2 = BCDin[2]; a3 = BCDin[3]

  // Notes on the sheet:
  //   Machen Sie Ihre Implementierung hier unten und verändern Sie nichts oberhalb dieser Mitteilung.
  //   Effectuez votre mise en œuvre ci-dessous et ne modifiez rien au-dessus de ce message.
endmodule

module segmentC (
  input  [3:0] BCDin,
  output seg_C
);

  wire not_1_out;

  not not_1 (not_1_out, BCDin[1]);
  or or_1 (seg_C, BCDin[0], not_1_out, BCDin[2]);

  // Other names for the same wires on the sheet: a0 = BCDin[0]; a1 = BCDin[1]; a2 = BCDin[2]; a3 = BCDin[3]

  // Notes on the sheet:
  //   Machen Sie Ihre Implementierung hier unten und verändern Sie nichts oberhalb dieser Mitteilung.
  //   Effectuez votre mise en œuvre ci-dessous et ne modifiez rien au-dessus de ce message.
endmodule

module segmentA (
  input  [3:0] BCDin,
  output seg_A
);

  wire xor_1_out, xor_2_out;

  xor xor_1 (xor_1_out, BCDin[0], BCDin[2]);
  xor xor_2 (xor_2_out, 1'b1, xor_1_out);
  or or_1 (seg_A, xor_2_out, BCDin[3], BCDin[1]);

  // Other names for the same wires on the sheet: a0 = BCDin[0]; a1 = BCDin[1]; a2 = BCDin[2]; a3 = BCDin[3]

  // Notes on the sheet:
  //   Machen Sie Ihre Implementierung hier unten und verändern Sie nichts oberhalb dieser Mitteilung.
  //   Effectuez votre mise en œuvre ci-dessous et ne modifiez rien au-dessus de ce message.
endmodule

module segmentD (
  input  [3:0] BCDin,
  output seg_D
);

  wire not_1_out, not_2_out, not_3_out, or_1_out, or_2_out, or_3_out;

  not not_1 (not_1_out, BCDin[2]);
  not not_2 (not_2_out, BCDin[0]);
  not not_3 (not_3_out, BCDin[1]);
  or or_1 (or_1_out, BCDin[0], BCDin[1], not_1_out);
  or or_2 (or_2_out, not_2_out, not_1_out, not_3_out);
  or or_3 (or_3_out, not_2_out, BCDin[1], BCDin[2], BCDin[3]);
  and and_1 (seg_D, or_1_out, or_2_out, or_3_out);

  // Other names for the same wires on the sheet: a0 = BCDin[0]; a1 = BCDin[1]; a2 = BCDin[2]; a3 = BCDin[3]

  // Notes on the sheet:
  //   Machen Sie Ihre Implementierung hier unten und verändern Sie nichts oberhalb dieser Mitteilung.
  //   Effectuez votre mise en œuvre ci-dessous et ne modifiez rien au-dessus de ce message.
endmodule

module segmentE (
  input  [3:0] BCDin,
  output seg_E
);

  wire and_1_out, xor_1_out, xor_2_out, xor_3_out;

  xor xor_1 (xor_1_out, BCDin[0], 1'b1);
  xor xor_2 (xor_2_out, BCDin[1], 1'b1);
  and and_1 (and_1_out, xor_2_out, BCDin[2]);
  xor xor_3 (xor_3_out, 1'b1, and_1_out);
  and and_2 (seg_E, xor_1_out, xor_3_out);

  // Other names for the same wires on the sheet: a0 = BCDin[0]; a1 = BCDin[1]; a2 = BCDin[2]; a3 = BCDin[3]

  // Notes on the sheet:
  //   Machen Sie Ihre Implementierung hier unten und verändern Sie nichts oberhalb dieser Mitteilung.
  //   Effectuez votre mise en œuvre ci-dessous et ne modifiez rien au-dessus de ce message.
endmodule

module segmentF (
  input  [3:0] BCDin,
  output seg_F
);

  wire nand_1_out, nand_2_out, nand_3_out, nand_4_out, nand_5_out, nand_6_out;

  nand nand_1 (nand_1_out, BCDin[0], BCDin[0]);
  nand nand_2 (nand_2_out, BCDin[1], BCDin[1]);
  nand nand_3 (nand_3_out, BCDin[3], BCDin[3]);
  nand nand_4 (nand_4_out, nand_1_out, nand_2_out);
  nand nand_5 (nand_5_out, nand_1_out, BCDin[2]);
  nand nand_6 (nand_6_out, BCDin[2], nand_2_out);
  nand nand_7 (seg_F, nand_4_out, nand_5_out, nand_6_out, nand_3_out);

  // Other names for the same wires on the sheet: a0 = BCDin[0]; a1 = BCDin[1]; a2 = BCDin[2]; a3 = BCDin[3]

  // Notes on the sheet:
  //   Machen Sie Ihre Implementierung hier unten und verändern Sie nichts oberhalb dieser Mitteilung.
  //   Effectuez votre mise en œuvre ci-dessous et ne modifiez rien au-dessus de ce message.
endmodule

module segmentG (
  input  [3:0] BCDin,
  output seg_G
);

  wire not_1_out, not_2_out, not_3_out, or_1_out, or_2_out, or_3_out, or_4_out;

  not not_1 (not_1_out, BCDin[1]);
  not not_2 (not_2_out, BCDin[0]);
  or or_1 (or_1_out, BCDin[1], BCDin[2]);
  not not_3 (not_3_out, BCDin[2]);
  or or_2 (or_2_out, not_1_out, not_2_out);
  or or_3 (or_3_out, or_1_out, BCDin[3]);
  or or_4 (or_4_out, not_3_out, or_2_out);
  and and_1 (seg_G, or_3_out, or_4_out);

  // Other names for the same wires on the sheet: a0 = BCDin[0]; a1 = BCDin[1]; a2 = BCDin[2]; a3 = BCDin[3]

  // Notes on the sheet:
  //   Machen Sie Ihre Implementierung hier unten und verändern Sie nichts oberhalb dieser Mitteilung.
  //   Effectuez votre mise en œuvre ci-dessous et ne modifiez rien au-dessus de ce message.
endmodule

module AdderTestBench (
);

  wire Adder8Bit_overflow, bcd_to_7_segment_decoder_2_p1, bcd_to_7_segment_decoder_3_p1,
       binary_to_bcd_converter_1_p2, comparator_1_eq, comparator_1_gt, comparator_1_lt, or_1_out;
  wire [7:0] Adder8Bit_sum, adder_1_out, Xin_sw8, Yin_sw8;

  DipSwitch Xin (
    .sw1(Xin_sw8[7]), .sw2(Xin_sw8[6]), .sw3(Xin_sw8[5]), .sw4(Xin_sw8[4]), .sw5(Xin_sw8[3]),
    .sw6(Xin_sw8[2]), .sw7(Xin_sw8[1]), .sw8(Xin_sw8[0]));
  DipSwitch Yin (
    .sw1(Yin_sw8[7]), .sw2(Yin_sw8[6]), .sw3(Yin_sw8[5]), .sw4(Yin_sw8[4]), .sw5(Yin_sw8[3]),
    .sw6(Yin_sw8[2]), .sw7(Yin_sw8[1]), .sw8(Yin_sw8[0]));
  EightBitAdder Adder8Bit (.Xin(Xin_sw8), .Yin(Yin_sw8), .Sum(Adder8Bit_sum), .Overflow(Adder8Bit_overflow));
  LED Overflow (.in(Adder8Bit_overflow));
  Adder adder_1 (.a(Yin_sw8), .b(Xin_sw8), .out(adder_1_out));  // open: cin, cout
  _7_Segment_Display seg100s ();  // open: g, f, a, b, e, d, c, dp
  _7_Segment_Display seg10s ();  // open: g, f, a, b, e, d, c, dp
  // BCD_to_7_Segment_decoder bcd_to_7_segment_decoder_1: pin names not known
  // BCD_to_7_Segment_decoder bcd_to_7_segment_decoder_2: pin names not known; wires that end beside it: bcd_to_7_segment_decoder_2_p1
  // Binary_to_BCD_converter #(.binvalue(8)) binary_to_bcd_converter_1: pin names not known; wires that end beside it: Adder8Bit_sum, binary_to_bcd_converter_1_p2, binary_to_bcd_converter_1_p2, bcd_to_7_segment_decoder_2_p1
  Comparator comparator_1 (
    .a(Adder8Bit_sum), .b(adder_1_out), .gt(comparator_1_gt), .eq(comparator_1_eq), .lt(comparator_1_lt));
  _7_Segment_Display seg1s ();  // open: g, f, a, b, e, d, c, dp
  // BCD_to_7_Segment_decoder bcd_to_7_segment_decoder_3: pin names not known; wires that end beside it: bcd_to_7_segment_decoder_3_p1, bcd_to_7_segment_decoder_3_p1
  or or_1 (or_1_out, comparator_1_gt, comparator_1_lt);
  // RGBLED Equal: pin names not known; wires that end beside it: or_1_out, comparator_1_eq
endmodule

module FullAdder (
  input  Xin,
  input  Yin,
  input  Cin,
  output Sum,
  output Cout
);

  wire and_1_out, and_2_out, and_3_out;

  xor xor_1 (Sum, Xin, Yin, Cin);
  and and_1 (and_1_out, Xin, Yin);
  and and_2 (and_2_out, Xin, Cin);
  and and_3 (and_3_out, Yin, Cin);
  or or_1 (Cout, and_1_out, and_2_out, and_3_out);

  // Notes on the sheet:
  //   Machen Sie Ihre Implementierung hier unten und verändern Sie nichts oberhalb dieser Mitteilung.
  //   Effectuez votre mise en œuvre ci-dessous et ne modifiez rien au-dessus de ce message.
endmodule

module EightBitAdder (
  input  [7:0] Xin,
  input  [7:0] Yin,
  output [7:0] Sum,
  output Overflow
);

  wire FULLADDER1_cout, FULLADDER2_cout, FULLADDER3_cout, FULLADDER4_cout, FULLADDER5_cout, FULLADDER6_cout,
       FULLADDER7_cout;

  FullAdder FULLADDER1 (.Xin(Xin[0]), .Yin(Yin[0]), .Cout(FULLADDER1_cout), .Sum(Sum[0]));  // open: Cin
  FullAdder FULLADDER2 (.Cin(FULLADDER1_cout), .Xin(Xin[1]), .Yin(Yin[1]), .Cout(FULLADDER2_cout), .Sum(Sum[1]));
  FullAdder FULLADDER3 (.Cin(FULLADDER2_cout), .Xin(Xin[2]), .Yin(Yin[2]), .Cout(FULLADDER3_cout), .Sum(Sum[2]));
  FullAdder FULLADDER4 (.Cin(FULLADDER3_cout), .Xin(Xin[3]), .Yin(Yin[3]), .Cout(FULLADDER4_cout), .Sum(Sum[3]));
  FullAdder FULLADDER5 (.Cin(FULLADDER4_cout), .Xin(Xin[4]), .Yin(Yin[4]), .Cout(FULLADDER5_cout), .Sum(Sum[4]));
  FullAdder FULLADDER6 (.Cin(FULLADDER5_cout), .Xin(Xin[5]), .Yin(Yin[5]), .Cout(FULLADDER6_cout), .Sum(Sum[5]));
  FullAdder FULLADDER7 (.Cin(FULLADDER6_cout), .Xin(Xin[6]), .Yin(Yin[6]), .Cout(FULLADDER7_cout), .Sum(Sum[6]));
  FullAdder FULLADDER8 (.Cin(FULLADDER7_cout), .Xin(Xin[7]), .Yin(Yin[7]), .Cout(Overflow), .Sum(Sum[7]));

  // Other names for the same wires on the sheet: X0 = Xin[0]; X1 = Xin[1]; X2 = Xin[2]; X3 = Xin[3]; X4 = Xin[4];
  //   X5 = Xin[5]; X6 = Xin[6]; X7 = Xin[7]; Y0 = Yin[0]; Y1 = Yin[1]; Y2 = Yin[2]; Y3 = Yin[3]; Y4 = Yin[4];
  //   Y5 = Yin[5]; Y6 = Yin[6]; Y7 = Yin[7]

  // Notes on the sheet:
  //   Machen Sie Ihre Implementierung hier unten und verändern Sie nichts oberhalb dieser Mitteilung.
  //   Effectuez votre mise en œuvre ci-dessous et ne modifiez rien au-dessus de ce message.
endmodule

module SubtractorTestBench (
);

  wire bcd_to_7_segment_decoder_2_p1, bcd_to_7_segment_decoder_3_p1, binary_to_bcd_converter_1_p2,
       comparator_1_eq, comparator_1_gt, comparator_1_lt, EBS_underflow, or_1_out;
  wire [7:0] EBS_sub, subtractor_1_out, Xin_sw8, Yin_sw8;

  DipSwitch Xin (
    .sw1(Xin_sw8[7]), .sw2(Xin_sw8[6]), .sw3(Xin_sw8[5]), .sw4(Xin_sw8[4]), .sw5(Xin_sw8[3]),
    .sw6(Xin_sw8[2]), .sw7(Xin_sw8[1]), .sw8(Xin_sw8[0]));
  DipSwitch Yin (
    .sw1(Yin_sw8[7]), .sw2(Yin_sw8[6]), .sw3(Yin_sw8[5]), .sw4(Yin_sw8[4]), .sw5(Yin_sw8[3]),
    .sw6(Yin_sw8[2]), .sw7(Yin_sw8[1]), .sw8(Yin_sw8[0]));
  EightBitSubtractor EBS (.Xin(Xin_sw8), .Yin(Yin_sw8), .Sub(EBS_sub), .Underflow(EBS_underflow));
  LED Underflow (.in(EBS_underflow));
  Subtractor subtractor_1 (.a(Xin_sw8), .b(Yin_sw8), .out(subtractor_1_out));  // open: bin, bout
  _7_Segment_Display seg100s ();  // open: g, f, a, b, e, d, c, dp
  _7_Segment_Display seg10s ();  // open: g, f, a, b, e, d, c, dp
  // BCD_to_7_Segment_decoder bcd_to_7_segment_decoder_1: pin names not known
  // BCD_to_7_Segment_decoder bcd_to_7_segment_decoder_2: pin names not known; wires that end beside it: bcd_to_7_segment_decoder_2_p1
  // Binary_to_BCD_converter #(.binvalue(8)) binary_to_bcd_converter_1: pin names not known; wires that end beside it: EBS_sub, binary_to_bcd_converter_1_p2, binary_to_bcd_converter_1_p2, bcd_to_7_segment_decoder_2_p1
  Comparator comparator_1 (
    .a(EBS_sub), .b(subtractor_1_out), .gt(comparator_1_gt), .eq(comparator_1_eq), .lt(comparator_1_lt));
  _7_Segment_Display seg1s ();  // open: g, f, a, b, e, d, c, dp
  // BCD_to_7_Segment_decoder bcd_to_7_segment_decoder_3: pin names not known; wires that end beside it: bcd_to_7_segment_decoder_3_p1, bcd_to_7_segment_decoder_3_p1
  or or_1 (or_1_out, comparator_1_gt, comparator_1_lt);
  // RGBLED Equal: pin names not known; wires that end beside it: or_1_out, comparator_1_eq
endmodule

module Fullsubtractor (
  input  Xin,
  input  Yin,
  input  Bin,
  output Sub,
  output Bout
);

  wire and_1_out, and_2_out, and_3_out, not_1_out;

  not not_1 (not_1_out, Xin);
  xor xor_1 (Sub, Xin, Yin, Bin);
  and and_1 (and_1_out, not_1_out, Yin);
  and and_2 (and_2_out, not_1_out, Bin);
  and and_3 (and_3_out, Yin, Bin);
  or or_1 (Bout, and_1_out, and_2_out, and_3_out);

  // Notes on the sheet:
  //   Machen Sie Ihre Implementierung hier unten und verändern Sie nichts oberhalb dieser Mitteilung.
  //   Effectuez votre mise en œuvre ci-dessous et ne modifiez rien au-dessus de ce message.
endmodule

module EightBitSubtractor (
  input  [7:0] Xin,
  input  [7:0] Yin,
  output [7:0] Sub,
  output Underflow
);

  wire FULLSUBTRACTOR1_bout, FULLSUBTRACTOR2_bout, FULLSUBTRACTOR3_bout, FULLSUBTRACTOR4_bout,
       FULLSUBTRACTOR5_bout, FULLSUBTRACTOR6_bout, FULLSUBTRACTOR7_bout;

  Fullsubtractor FULLSUBTRACTOR1 (.Xin(Xin[0]), .Yin(Yin[0]), .Bout(FULLSUBTRACTOR1_bout), .Sub(Sub[0]));  // open: Bin
  Fullsubtractor FULLSUBTRACTOR2 (
    .Bin(FULLSUBTRACTOR1_bout), .Xin(Xin[1]), .Yin(Yin[1]), .Bout(FULLSUBTRACTOR2_bout), .Sub(Sub[1]));
  Fullsubtractor FULLSUBTRACTOR3 (
    .Bin(FULLSUBTRACTOR2_bout), .Xin(Xin[2]), .Yin(Yin[2]), .Bout(FULLSUBTRACTOR3_bout), .Sub(Sub[2]));
  Fullsubtractor FULLSUBTRACTOR4 (
    .Bin(FULLSUBTRACTOR3_bout), .Xin(Xin[3]), .Yin(Yin[3]), .Bout(FULLSUBTRACTOR4_bout), .Sub(Sub[3]));
  Fullsubtractor FULLSUBTRACTOR5 (
    .Bin(FULLSUBTRACTOR4_bout), .Xin(Xin[4]), .Yin(Yin[4]), .Bout(FULLSUBTRACTOR5_bout), .Sub(Sub[4]));
  Fullsubtractor FULLSUBTRACTOR6 (
    .Bin(FULLSUBTRACTOR5_bout), .Xin(Xin[5]), .Yin(Yin[5]), .Bout(FULLSUBTRACTOR6_bout), .Sub(Sub[5]));
  Fullsubtractor FULLSUBTRACTOR7 (
    .Bin(FULLSUBTRACTOR6_bout), .Xin(Xin[6]), .Yin(Yin[6]), .Bout(FULLSUBTRACTOR7_bout), .Sub(Sub[6]));
  Fullsubtractor FULLSUBTRACTOR8 (
    .Bin(FULLSUBTRACTOR7_bout), .Xin(Xin[7]), .Yin(Yin[7]), .Bout(Underflow), .Sub(Sub[7]));

  // Other names for the same wires on the sheet: X0 = Xin[0]; X1 = Xin[1]; X2 = Xin[2]; X3 = Xin[3]; X4 = Xin[4];
  //   X5 = Xin[5]; X6 = Xin[6]; X7 = Xin[7]; Y0 = Yin[0]; Y1 = Yin[1]; Y2 = Yin[2]; Y3 = Yin[3]; Y4 = Yin[4];
  //   Y5 = Yin[5]; Y6 = Yin[6]; Y7 = Yin[7]

  // Notes on the sheet:
  //   Machen Sie Ihre Implementierung hier unten und verändern Sie nichts oberhalb dieser Mitteilung.
  //   Effectuez votre mise en œuvre ci-dessous et ne modifiez rien au-dessus de ce message.
endmodule

module OneBitMultiplexer (
  input  AddIn,
  input  SubIn,
  input  SelectSub,
  output ToDisplay
);

  wire and_1_out, and_2_out, not_1_out;

  not not_1 (not_1_out, SelectSub);
  and and_1 (and_1_out, AddIn, not_1_out);
  and and_2 (and_2_out, SubIn, SelectSub);
  or or_1 (ToDisplay, and_1_out, and_2_out);

  // Notes on the sheet:
  //   Machen Sie Ihre Implementierung hier unten und verändern Sie nichts oberhalb dieser Mitteilung.
  //   Effectuez votre mise en œuvre ci-dessous et ne modifiez rien au-dessus de ce message.
endmodule

module EightBitMultiplexer (
  input  [7:0] AddIn,
  input  [7:0] SubIn,
  input  SelectSub,
  output [7:0] ToDisplay
);

  OneBitMultiplexer OneBitPultiplexerBit0 (
    .SubIn(SubIn[0]), .SelectSub(SelectSub), .AddIn(AddIn[0]), .ToDisplay(ToDisplay[0]));
  OneBitMultiplexer OneBitPultiplexerBit1 (
    .SubIn(SubIn[1]), .SelectSub(SelectSub), .AddIn(AddIn[1]), .ToDisplay(ToDisplay[1]));
  OneBitMultiplexer OneBitPultiplexerBit2 (
    .SubIn(SubIn[2]), .SelectSub(SelectSub), .AddIn(AddIn[2]), .ToDisplay(ToDisplay[2]));
  OneBitMultiplexer OneBitPultiplexerBit3 (
    .SubIn(SubIn[3]), .SelectSub(SelectSub), .AddIn(AddIn[3]), .ToDisplay(ToDisplay[3]));
  OneBitMultiplexer OneBitPultiplexerBit4 (
    .SubIn(SubIn[4]), .SelectSub(SelectSub), .AddIn(AddIn[4]), .ToDisplay(ToDisplay[4]));
  OneBitMultiplexer OneBitPultiplexerBit5 (
    .SubIn(SubIn[5]), .SelectSub(SelectSub), .AddIn(AddIn[5]), .ToDisplay(ToDisplay[5]));
  OneBitMultiplexer OneBitPultiplexerBit6 (
    .SubIn(SubIn[6]), .SelectSub(SelectSub), .AddIn(AddIn[6]), .ToDisplay(ToDisplay[6]));
  OneBitMultiplexer OneBitPultiplexerBit7 (
    .SubIn(SubIn[7]), .SelectSub(SelectSub), .AddIn(AddIn[7]), .ToDisplay(ToDisplay[7]));

  // Notes on the sheet:
  //   Machen Sie Ihre Implementierung hier unten und verändern Sie nichts oberhalb dieser Mitteilung.
  //   Effectuez votre mise en œuvre ci-dessous et ne modifiez rien au-dessus de ce message.
endmodule

module AdderAndSubtractor (
);

  wire AdderEightBit_overflow, and_1_out, Clk_out, overunder_p2, s_r_ff_1_q, s_r_ff_1_qn, SelectAdd_out,
       SelectSub_out, SubtractorEightBit_underflow;
  wire [3:0] bcd_to_7_segment_decoder_1_p1, bcd_to_7_segment_decoder_2_p1, bcd_to_7_segment_decoder_3_p1;
  wire [7:0] AdderEightBit_sum, Mux_todisplay, SubtractorEightBit_sub, Xin_sw8, Yin_sw8;

  DipSwitch Xin (
    .sw1(Xin_sw8[7]), .sw2(Xin_sw8[6]), .sw3(Xin_sw8[5]), .sw4(Xin_sw8[4]), .sw5(Xin_sw8[3]),
    .sw6(Xin_sw8[2]), .sw7(Xin_sw8[1]), .sw8(Xin_sw8[0]));
  DipSwitch Yin (
    .sw1(Yin_sw8[7]), .sw2(Yin_sw8[6]), .sw3(Yin_sw8[5]), .sw4(Yin_sw8[4]), .sw5(Yin_sw8[3]),
    .sw6(Yin_sw8[2]), .sw7(Yin_sw8[1]), .sw8(Yin_sw8[0]));
  EightBitAdder AdderEightBit (
    .Xin(Xin_sw8), .Yin(Yin_sw8), .Sum(AdderEightBit_sum), .Overflow(AdderEightBit_overflow));
  EightBitSubtractor SubtractorEightBit (
    .Xin(Xin_sw8), .Yin(Yin_sw8), .Sub(SubtractorEightBit_sub), .Underflow(SubtractorEightBit_underflow));
  and and_1 (and_1_out, AdderEightBit_overflow, ~s_r_ff_1_q);  // AND_Gate
  S_R_Flip_Flop s_r_ff_1 (
    .S(SelectSub_out), .R(SelectAdd_out), .clk(Clk_out), .Q(s_r_ff_1_q), .Qn(s_r_ff_1_qn));  // open: reset, preset
  Button SelectSub (.out(SelectSub_out));
  Button SelectAdd (.out(SelectAdd_out));
  Clock Clk (.out(Clk_out));
  // RGBLED overunder: pin names not known; wires that end beside it: and_1_out, overunder_p2
  and and_2 (overunder_p2, SubtractorEightBit_underflow, s_r_ff_1_q);
  EightBitMultiplexer Mux (
    .AddIn(AdderEightBit_sum), .SelectSub(s_r_ff_1_q), .SubIn(SubtractorEightBit_sub),
    .ToDisplay(Mux_todisplay));
  LED SubSelected (.in(s_r_ff_1_q));
  LED AddSelected (.in(s_r_ff_1_qn));
  _7_Segment_Display Seg100s ();  // open: g, f, a, b, e, d, c, dp
  _7_Segment_Display Seg10s ();  // open: g, f, a, b, e, d, c, dp
  // BCD_to_7_Segment_decoder bcd_to_7_segment_decoder_1: pin names not known; wires that end beside it: bcd_to_7_segment_decoder_1_p1
  // BCD_to_7_Segment_decoder bcd_to_7_segment_decoder_2: pin names not known; wires that end beside it: bcd_to_7_segment_decoder_2_p1
  _7_Segment_Display Seg1s ();  // open: g, f, a, b, e, d, c, dp
  // BCD_to_7_Segment_decoder bcd_to_7_segment_decoder_3: pin names not known; wires that end beside it: bcd_to_7_segment_decoder_3_p1
  BinToBcd bintobcd_1 (
    .BinIn(Mux_todisplay), .Ones(bcd_to_7_segment_decoder_3_p1), .Hundreds(bcd_to_7_segment_decoder_1_p1),
    .Tens(bcd_to_7_segment_decoder_2_p1));

  // Notes on the sheet:
  //   red: Overflow
  //   blue: Underflow
endmodule

module Add3 (
  input  [3:0] BcdIn,
  output [3:0] BcdCorrected
);

  wire and_1_out, and_2_out, and_3_out, and_4_out, and_5_out, and_6_out, and_7_out, or_1_out, or_2_out,
       or_3_out;

  and and_1 (and_1_out, ~BcdIn[0], ~BcdIn[2], BcdIn[3]);  // AND_Gate
  and and_2 (and_2_out, ~BcdIn[0], BcdIn[1], BcdIn[2]);  // AND_Gate
  and and_3 (and_3_out, ~BcdIn[3], ~BcdIn[2], BcdIn[0]);  // AND_Gate
  or or_1 (or_1_out, ~BcdIn[0], ~BcdIn[3]);  // OR_Gate
  or or_2 (or_2_out, BcdIn[1], BcdIn[3]);
  or or_3 (or_3_out, BcdIn[0], ~BcdIn[1], ~BcdIn[2]);  // OR_Gate
  and and_4 (and_4_out, BcdIn[0], BcdIn[3]);
  and and_5 (and_5_out, BcdIn[2], ~BcdIn[0], ~BcdIn[1]);  // AND_Gate
  and and_6 (and_6_out, BcdIn[0], BcdIn[2]);
  and and_7 (and_7_out, BcdIn[2], BcdIn[1]);
  or or_4 (BcdCorrected[0], and_1_out, and_2_out, and_3_out);
  and and_8 (BcdCorrected[1], or_1_out, or_2_out, or_3_out);
  or or_5 (BcdCorrected[2], and_4_out, and_5_out);
  or or_6 (BcdCorrected[3], and_6_out, and_7_out, BcdIn[3]);

  // Notes on the sheet:
  //   Machen Sie Ihre Implementierung hier unten und verändern Sie nichts oberhalb dieser Mitteilung.
  //   Effectuez votre mise en œuvre ci-dessous et ne modifiez rien au-dessus de ce message.
endmodule

module BinToBcd (
  input  [7:0] BinIn,
  output [3:0] Ones,
  output [3:0] Tens,
  output [3:0] Hundreds
);

  wire [2:0] Add3_1_bcdcorrected, Add3_2_bcdcorrected, Add3_6_bcdcorrected;
  wire [2:1] Add3_2_bcdcorrected_2;
  wire [3:0] Add3_3_bcdcorrected, Add3_4_bcdcorrected;

  Add3 Add3_1 (.BcdIn({1'b0, BinIn[7:5]}), .BcdCorrected({Add3_2_bcdcorrected_2[2], Add3_1_bcdcorrected}));
  Add3 Add3_2 (.BcdIn({Add3_1_bcdcorrected, BinIn[4]}), .BcdCorrected({Add3_2_bcdcorrected_2[1], Add3_2_bcdcorrected}));
  Add3 Add3_3 (.BcdIn({Add3_2_bcdcorrected, BinIn[3]}), .BcdCorrected(Add3_3_bcdcorrected));
  Add3 Add3_4 (.BcdIn({Add3_3_bcdcorrected[2:0], BinIn[2]}), .BcdCorrected(Add3_4_bcdcorrected));
  Add3 Add3_6 (
    .BcdIn({1'b0, Add3_2_bcdcorrected_2, Add3_3_bcdcorrected[3]}),
    .BcdCorrected({Hundreds[1], Add3_6_bcdcorrected}));
  Add3 Add3_5 (.BcdIn({Add3_4_bcdcorrected[2:0], BinIn[1]}), .BcdCorrected({Tens[0], Ones[3:1]}));
  Add3 Add3_7 (.BcdIn({Add3_6_bcdcorrected, Add3_4_bcdcorrected[3]}), .BcdCorrected({Hundreds[0], Tens[3:1]}));

  assign Hundreds[3:2] = 2'b00;
  assign Ones[0] = BinIn[0];

  // Other names for the same wires on the sheet: Ones0 = BinIn[0]

  // Notes on the sheet:
  //   Machen Sie Ihre Implementierung hier unten und verändern Sie nichts oberhalb dieser Mitteilung.
  //   Effectuez votre mise en œuvre ci-dessous et ne modifiez rien au-dessus de ce message.
endmodule
